# Fritzing sketch Circuit (saved by Fritzing 0.8.3b)

parts:
  JACK1 = 2.1mm Barrel Jack with Terminal Block
  Part1 = Arduino Uno (Rev3)
  Q1 = MOSFET-NCHANNEL [package=to220v]
  R1 = Resistor [tolerance=±5% resistance=10k package="0805 [SMD]"]
  S1 = Round Pushbutton
  LED1 = Super Flux LED blue [color=Blue]
  D1 = Diode [package=diode-1n4148]  # not connected

nets:
  N1: JACK1.POS, Part1.VIN, LED1.anode
  N2: JACK1.NEG, Part1.GND, Q1.S, R1.Pin_1, S1.leg0
  N3: Part1.D2, Q1.G, R1.Pin_0
  N4: Part1.D4, S1.leg1
  N5: Q1.D, LED1.cathode

notes:
  Circuit for the Strobe Alert Project.
  Basic Idea is to trigger a strobe light - represented as a single LED in this diagram - using a mosfet and Arduino. The Arduino
  has a button to trigger the mosfet gate and also uses serial
  communication and a command set as a trigger.
  On the other end of the serial communication is a simple
  program that looks for alert states.
  Pin 4 is set to INPUT_PULLUP in this situation. I did it this way because I forgot to bring a resistor of appropriate size to the hackathon. (See http://arduino.cc/en/Tutorial/InputPullupSerial)
